# Fritzing sketch Design (saved by Fritzing 0.9.6b)
circuit board: 9.14236cm x 5.31215cm

parts:
  R2 = Trimmer Potentiometer [maximum_resistance=10kΩ package=THT]
  R3 = Resistor [tolerance=±5% resistance=220 package="2512 [SMD]"]
  Part2 = MicroSD Card Module
  DS1 = DS18B20 1-Wire Temperature Sensor [part_number=DS18B20]
  ZS-042_RTC1 = ZS-042 RTC Module
  R1 = Resistor [tolerance=±5% resistance=4.7k package="2512 [SMD]"]
  Arduino1 = Arduino Mini (Rev5)
  C1 = Electrolytic Capacitor [capacitance=0.22mF voltage=10V package="100 mil [THT, electrolytic]"]
  JP1 = USB_MICROB_PLUG [package=micro-b-th]
  U1 = LCD-16X2 [package=lcd-16x2_nosilk]

nets:
  VCC: R2.leg1, R3.Pin_1, Part2.VCC, DS1.VDD, ZS-042_RTC1.VCC, R1.Pin_0, Arduino1.5V, C1.+, JP1.VCC, U1.VDD
  N1: R2.wiper, U1.VO
  GND: R2.leg2, Part2.GND, DS1.GND, ZS-042_RTC1.GND, Arduino1.GND, C1.-, JP1.GND, U1.VSS, U1.R_W, U1.K
  N2: R3.Pin_0, U1.A
  N3: Part2.MISO, Arduino1.D12
  N4: Part2.MOSI, Arduino1.D11_PWM
  N5: Part2.SCK, Arduino1.D13
  N6: Part2.CS, Arduino1.D7
  N7: DS1.DQ, R1.Pin_1, Arduino1.D6_PWM
  N8: ZS-042_RTC1.SDA, Arduino1.A4
  N9: ZS-042_RTC1.SCL, Arduino1.A5
  N10: ZS-042_RTC1.SQW, Arduino1.D2
  N11: Arduino1.D8, U1.E
  N12: Arduino1.D9_PWM, U1.RS
  N13: Arduino1.A3, U1.DB7
  N14: Arduino1.A2, U1.DB6
  N15: Arduino1.A1, U1.DB5
  N16: Arduino1.A0, U1.DB4
